# Fritzing sketch Hall_Schematic (saved by Fritzing 0.9.3b)
breadboards: 1

parts:
  LED1 = LED - 5mm [color="Red (633nm)" package="5 mm [THT]"]  # not connected
  R1 = Resistor [tolerance=±5% resistance=220 package=THT]
  U3 = ESP 32 DEVKIT DOIT
  LED2 = LED - 5mm [color="Yellow (595nm)" package="5 mm [THT]"]
  R2 = Resistor [tolerance=±5% resistance=220 package=THT]

nets:
  N1: R1.Pin_1, U3.D5, U3.RX2, U3.D4, U3.GND, LED2.cathode, R2.Pin_1
  N2: LED2.anode, R2.Pin_0
