# Fritzing sketch Touch_Schematic (saved by Fritzing 0.9.3b)
breadboards: 1

parts:
  LED1 = LED - 5mm [color="Red (633nm)" package="5 mm [THT]"]  # not connected
  R1 = Resistor [tolerance=±5% resistance=220 package=THT]
  U3 = ESP 32 DEVKIT DOIT
  LED2 = LED - 5mm [color="Blue (430nm)" package="5 mm [THT]"]
  LED3 = LED - 5mm [color="Yellow (585nm)" package="5 mm [THT]"]
  R2 = Resistor [tolerance=±5% resistance=220 package=THT]
  R3 = Resistor [tolerance=±5% resistance=220 package=THT]

nets:
  N1: R1.Pin_1, U3.D22, U3.D18, U3.RX2, U3.D4, U3.GND, LED2.cathode, LED3.cathode, R2.Pin_1
  N2: U3.D19, R3.Pin_1
  N3: LED2.anode, R2.Pin_0
  N4: LED3.anode, R3.Pin_0

notes:
  Touch sensor (ON)
  Touch sensor (OFF)
