# Fritzing sketch WifiLEDManip (saved by Fritzing 0.9.3b)
breadboards: 1

parts:
  U2 = ESP 32 DEVKIT DOIT
  R1 = Resistor [tolerance=±5% resistance=220 package=THT]
  R2 = Resistor [tolerance=±5% resistance=220 package=THT]

nets:
  N1: U2.CMD, R1.Pin_0, R2.Pin_0
